# Fritzing sketch kos-v1 (saved by Fritzing 0.9.9b)
circuit board: 13.1938cm x 7.15711cm
breadboards: 1

parts:
  S1 = Kailh Choc Switch [package=THT]
  S2 = Kailh Choc Switch [package=THT]
  S3 = Kailh Choc Switch [package=THT]
  S4 = Kailh Choc Switch [package=THT]
  S5 = Kailh Choc Switch [package=THT]
  S6 = Kailh Choc Switch [package=THT]
  S7 = Kailh Choc Switch [package=THT]
  S8 = Kailh Choc Switch [package=THT]
  S9 = Kailh Choc Switch [package=THT]
  S10 = Kailh Choc Switch [package=THT]
  S11 = Kailh Choc Switch [package=THT]
  S12 = Kailh Choc Switch [package=THT]
  S13 = Kailh Choc Switch [package=THT]
  S14 = Kailh Choc Switch [package=THT]
  S15 = Kailh Choc Switch [package=THT]
  D1 = Rectifier Diode [package="Melf DO-213 AA [SMD]"]
  D2 = Rectifier Diode [package="Melf DO-213 AA [SMD]"]
  D3 = Rectifier Diode [package="Melf DO-213 AA [SMD]"]
  D4 = Rectifier Diode [package="Melf DO-213 AA [SMD]"]
  D5 = Rectifier Diode [package="Melf DO-213 AA [SMD]"]
  D6 = Rectifier Diode [package="Melf DO-213 AA [SMD]"]
  D7 = Rectifier Diode [package="Melf DO-213 AA [SMD]"]
  D8 = Rectifier Diode [package="Melf DO-213 AA [SMD]"]
  D9 = Rectifier Diode [package="Melf DO-213 AA [SMD]"]
  D10 = Rectifier Diode [package="Melf DO-213 AA [SMD]"]
  D11 = Rectifier Diode [package="Melf DO-213 AA [SMD]"]
  D12 = Rectifier Diode [package="Melf DO-213 AA [SMD]"]
  D19 = Rectifier Diode [package="Melf DO-213 AA [SMD]"]
  D20 = Rectifier Diode [package="Melf DO-213 AA [SMD]"]
  D25 = Rectifier Diode [package="Melf DO-213 AA [SMD]"]
  S27 = Kailh Choc Switch [package=THT]
  S29 = Kailh Choc Switch [package=THT]
  S30 = Kailh Choc Switch [package=THT]
  S17 = Kailh Choc Switch [package=THT]
  S19 = Kailh Choc Switch [package=THT]
  S22 = Kailh Choc Switch [package=THT]
  S26 = Kailh Choc Switch [package=THT]
  S18 = Kailh Choc Switch [package=THT]
  S24 = Kailh Choc Switch [package=THT]
  S28 = Kailh Choc Switch [package=THT]
  S25 = Kailh Choc Switch [package=THT]
  S16 = Kailh Choc Switch [package=THT]
  S23 = Kailh Choc Switch [package=THT]
  S20 = Kailh Choc Switch [package=THT]
  S21 = Kailh Choc Switch [package=THT]
  D16 = Rectifier Diode [package="Melf DO-213 AA [SMD]"]
  D27 = Rectifier Diode [package="Melf DO-213 AA [SMD]"]
  D30 = Rectifier Diode [package="Melf DO-213 AA [SMD]"]
  D18 = Rectifier Diode [package="Melf DO-213 AA [SMD]"]
  D17 = Rectifier Diode [package="Melf DO-213 AA [SMD]"]
  D26 = Rectifier Diode [package="Melf DO-213 AA [SMD]"]
  D23 = Rectifier Diode [package="Melf DO-213 AA [SMD]"]
  D21 = Rectifier Diode [package="Melf DO-213 AA [SMD]"]
  D28 = Rectifier Diode [package="Melf DO-213 AA [SMD]"]
  D29 = Rectifier Diode [package="Melf DO-213 AA [SMD]"]
  D22 = Rectifier Diode [package="Melf DO-213 AA [SMD]"]
  D24 = Rectifier Diode [package="Melf DO-213 AA [SMD]"]
  Pad13 = Pad [width=5 height=2 connect=center]  # not connected
  Pad14 = Pad [width=5 height=2 connect=center]
  Pad15 = Pad [width=5 height=2 connect=center]
  Pad16 = Pad [width=5 height=2 connect=center]
  Pad17 = Pad [width=5 height=2 connect=center]
  Pad18 = Pad [width=5 height=2 connect=center]  # not connected
  Pad19 = Pad [width=5 height=2 connect=center]  # not connected
  Pad20 = Pad [width=5 height=2 connect=center]
  Pad21 = Pad [width=5 height=2 connect=center]  # not connected
  Pad22 = Pad [width=5 height=2 connect=center]
  Pad23 = Pad [width=5 height=2 connect=center]
  Pad24 = Pad [width=5 height=2 connect=center]
  Pad1 = Pad [width=5 height=2 connect=center]  # not connected
  Pad2 = Pad [width=5 height=2 connect=center]  # not connected
  Pad3 = Pad [width=5 height=2 connect=center]  # not connected
  Pad4 = Pad [width=5 height=2 connect=center]  # not connected
  Pad5 = Pad [width=5 height=2 connect=center]  # not connected
  Pad6 = Pad [width=5 height=2 connect=center]
  Pad7 = Pad [width=5 height=2 connect=center]
  Pad8 = Pad [width=5 height=2 connect=center]
  Pad9 = Pad [width=5 height=2 connect=center]
  Pad10 = Pad [width=5 height=2 connect=center]
  Pad11 = Pad [width=5 height=2 connect=center]
  Pad12 = Pad [width=5 height=2 connect=center]
  Pad25 = Pad [width=5 height=2 connect=center]
  Pad26 = Pad [width=5 height=2 connect=center]
  Pad27 = Pad [width=5 height=2 connect=center]
  J1 = female pin header, 3 pins [form="♀ (female)"]
  D13 = Rectifier Diode [package="Melf DO-213 AA [SMD]"]
  D14 = Rectifier Diode [package="Melf DO-213 AA [SMD]"]
  D15 = Rectifier Diode [package="Melf DO-213 AA [SMD]"]
  Pad28 = Pad [width=5 height=2 connect=center]
  Pad29 = Pad [width=5 height=2 connect=center]
  Pad30 = Pad [width=5 height=2 connect=center]
  J2 = female pin header, 2 pins [form="♀ (female)"]
  J3 = female pin header, 2 pins [form="♀ (female)"]
  J4 = female pin header, 2 pins [form="♀ (female)"]
  J5 = female pin header, 2 pins [form="♀ (female)"]
  J6 = female pin header, 2 pins [form="♀ (female)"]
  J7 = female pin header, 2 pins [form="♀ (female)"]
  J8 = female pin header, 2 pins [form="♀ (female)"]
  J9 = female pin header, 2 pins [form="♀ (female)"]
  J10 = female pin header, 2 pins [form="♀ (female)"]
  J11 = female pin header, 2 pins [form="♀ (female)"]
  J12 = female pin header, 2 pins [form="♀ (female)"]
  J13 = female pin header, 2 pins [form="♀ (female)"]
  J14 = female pin header, 2 pins [form="♀ (female)"]
  J15 = female pin header, 2 pins [form="♀ (female)"]
  J16 = female pin header, 2 pins [form="♀ (female)"]

nets:
  N1: S1.leg0, S7.leg0, S13.leg0, Pad24.pad
  N2: S1.leg1, D1.anode, S27.leg1, D16.anode, J2.pin2
  N3: S2.leg0, S8.leg0, S14.leg0, Pad20.pad
  N4: S2.leg1, D2.anode, S17.leg1, D27.anode, J3.pin2
  N5: S3.leg0, S9.leg0, S15.leg0, Pad15.pad
  N6: S3.leg1, D3.anode, S28.leg1, D30.anode, J4.pin2
  N7: S4.leg0, S10.leg0, Pad23.pad
  N8: S4.leg1, D4.anode, S24.leg1, D18.anode, J5.pin2
  N9: S5.leg0, S11.leg0, Pad22.pad
  N10: S5.leg1, D5.anode, S25.leg1, D28.anode, J6.pin2
  N11: S6.leg0, S12.leg0, Pad14.pad
  N12: S6.leg1, D6.anode, S16.leg1, D22.anode, J7.pin2
  N13: S7.leg1, D7.anode, S29.leg1, D17.anode, J13.pin2
  N14: S8.leg1, D8.anode, S30.leg1, D26.anode, J12.pin2
  N15: S9.leg1, D9.anode, S19.leg1, D23.anode, J11.pin2
  N16: S10.leg1, D10.anode, S22.leg1, D21.anode, J10.pin2
  N17: S11.leg1, D11.anode, S26.leg1, D29.anode, J9.pin2
  N18: S12.leg1, D12.anode, S18.leg1, D24.anode, J8.pin2
  N19: S13.leg1, D19.anode, S23.leg1, D13.anode, J16.pin2
  N20: S14.leg1, D20.anode, S20.leg1, D14.anode, J15.pin2
  N21: S15.leg1, D25.anode, S21.leg1, D15.anode, J14.pin2
  N22: D1.cathode, D2.cathode, D3.cathode, D4.cathode, D5.cathode, D6.cathode, D16.cathode, D27.cathode, D30.cathode, D18.cathode, D28.cathode, D22.cathode, Pad16.pad, Pad26.pad, J1.pin1, Pad28.pad, J2.pin1, J3.pin1, J4.pin1, J5.pin1, J6.pin1, J7.pin1
  N23: D7.cathode, D8.cathode, D9.cathode, D10.cathode, D11.cathode, D12.cathode, D17.cathode, D26.cathode, D23.cathode, D21.cathode, D29.cathode, D24.cathode, Pad17.pad, Pad25.pad, J1.pin2, Pad29.pad, J8.pin1, J9.pin1, J10.pin1, J11.pin1, J12.pin1, J13.pin1
  N24: D19.cathode, D20.cathode, D25.cathode, Pad12.pad, Pad27.pad, J1.pin3, D13.cathode, D14.cathode, D15.cathode, Pad30.pad, J14.pin1, J15.pin1, J16.pin1
  N25: S27.leg0, S29.leg0, S23.leg0, Pad11.pad
  N26: S30.leg0, S17.leg0, S20.leg0, Pad10.pad
  N27: S19.leg0, S28.leg0, S21.leg0, Pad9.pad
  N28: S22.leg0, S24.leg0, Pad6.pad
  N29: S26.leg0, S25.leg0, Pad7.pad
  N30: S18.leg0, S16.leg0, Pad8.pad

notes:
  Kos v1.0

custom parts:
  Kailh Choc Switch: A generic pushbutton.
